// Logisim project main.circ as structural Verilog: 1 circuit, main circuit main
module main (
  input  in_1
);

  wire not_1_out, or_1_out, or_2_out, or_3_out, or_4_out, or_5_out;

  not not_1 (not_1_out, in_1);
  or or_1 (or_1_out, in_1, not_1_out);
  or or_2 (or_2_out, in_1, not_1_out);
  or or_3 (or_3_out, in_1, not_1_out);
  or or_4 (or_4_out, in_1, not_1_out);
  or or_5 (or_5_out, in_1, not_1_out);
  LED led_1 (.in(or_1_out));
  LED led_2 (.in(or_2_out));
  LED led_3 (.in(or_3_out));
  LED led_4 (.in(or_4_out));
  LED led_5 (.in(or_5_out));

  // Notes on the sheet:
  //   el circuito
  //   ROJO AUTO
  //   AMARILLO AUTO
  //   VERDE AUTO
  //   ROJO PEATON
  //   VERDE PEATON
endmodule
